# Fritzing sketch first-exoeriment (saved by Fritzing 1.0.6)
breadboards: 1

parts:
  Part1 = Arduino Uno (Rev3)
  U1 = SN74LS14N [package="DIP14 [THT]"]
  Oscilloscope1 = Oscilloscope [volts/div=1V time/div=10ms ch1_offset=0V ch2_offset=0V ch3_offset=0V ch4_offset=0V ch1_volts/div=5V ch2_volts/div=5V ch3_volts/div=5V ch4_volts/div=5V horizontal_position=0s]
  R1 = 6mm Trimmer Potentiometer [maximum_resistance=10kΩ knob_status=50% power=0.5W package=THT]

nets:
  GND: Part1.GND, U1.GND, Oscilloscope1.COM_Probe, R1.leg2
  5V: Part1.5V, U1.VCC, R1.leg1
  N1: U1.1A, Oscilloscope1.V1_Probe, R1.wiper
